# Fritzing sketch submarine (saved by Fritzing 0.9.2b)
breadboards: 1

parts:
  Bottom = Basic Servo
  U1 = L9110 H-bridge module [part_number="L9110 H-bridge"]
  Navigation_body_IR_receiver = IR Receiver Breakout [package=PCB]
  6_40_V = Battery Holders [package=battery-aa]
  Part1 = Arduino Nano (Rev3.0)
  Ballast = DC Motor
  Propeller = DC Motor
  4_80_V = Battery Holders [package=battery-aa]
  4_80_V_2 = Battery Holders [package=battery-aa]
  Top = Basic Servo
  6_40_V_2 = Battery Holders [package=battery-aa]
  6_40_V_3 = Battery Holders [package=battery-aa]
  Front = Basic Servo
  Right = Basic Servo
  4_80_V_3 = Battery Holders [package=battery-aa]
  Left = Basic Servo
  6_40_V_4 = Battery Holders [package=battery-aa]
  Part2 = Humidity Sensor - HIH-4030 Breakout

nets:
  N1: Bottom.gnd, 4_80_V.-
  N2: Bottom.vcc, 4_80_V.+
  N3: Bottom.pulse, Part1.D2
  N4: U1.B-IA, Part1.D8
  N5: U1.B-IB, Part1.D7
  N6: U1.GND, 6_40_V.-
  N7: U1.VCC, 6_40_V.+
  N8: U1.A-IA, Part1.D10
  N9: U1.A-IB, Part1.D9
  N10: U1.MOTOR_A-A, Ballast.pin_1
  N11: U1.MOTOR_A-B, Ballast.pin_2
  N12: U1.MOTOR_B-A, Propeller.pin_2
  N13: U1.MOTOR_B-B, Propeller.pin_1
  GND: Navigation_body_IR_receiver.GND, Part1.GND, 6_40_V_4.-, Part2.GND
  N14: Navigation_body_IR_receiver.OUT, Part1.D11/MOSI
  VCC: Navigation_body_IR_receiver.VCC, Part1.5V
  N15: Part1.D3, Top.pulse
  N16: Part1.D4, Left.pulse
  N17: Part1.D5, Right.pulse
  N18: Part1.D6, Front.pulse
  N19: Part1.VIN, 6_40_V_4.+
  N20: Part1.A1, Part2.OUT
  3V3: Part1.3V3, Part2.VCC
  N21: 4_80_V_2.-, Top.gnd
  N22: 4_80_V_2.+, Top.vcc
  N23: 6_40_V_2.-, Right.gnd
  N24: 6_40_V_2.+, Right.vcc
  N25: 6_40_V_3.-, Front.gnd
  N26: 6_40_V_3.+, Front.vcc
  N27: 4_80_V_3.-, Left.gnd
  N28: 4_80_V_3.+, Left.vcc

notes:
  Rudders
  Hydroplanes
